# Fritzing sketch Glow2019 (saved by Fritzing 0.9.3b)
breadboards: 1

parts:
  Micro = Arduino Uno (Rev3)
  PIR1 = PIR sensor
  J1 = Screw terminal - 2 pins [package=THT]
  LPD8806_RGB_LED_Strip1 = LPD8806 RGB LED Strip
  V1 = DC Power [voltage=5]
  Pololu_A1 = Pololu A4988 [package=SO16]
  M1 = Stepper Motor - Bipolar
  C1 = Capacitor Polarized [package=panasonic_c]

nets:
  N1: Micro.D8, PIR1.SIG
  GND: Micro.GND, PIR1.GND, J1.pin1, LPD8806_RGB_LED_Strip1.GND, V1.V-, Pololu_A1.GND, C1.-
  N2: Micro.D4, LPD8806_RGB_LED_Strip1.DI, LPD8806_RGB_LED_Strip1.CI
  N3: Micro.D5_PWM, Pololu_A1.DIR
  N4: Micro.D6_PWM, Pololu_A1.STEP
  VDD: Micro.5V, PIR1.VDD, J1.pin2, Pololu_A1.VDD
  N5: LPD8806_RGB_LED_Strip1.+5V, V1.V+, Pololu_A1.VMOT, C1.+
  N6: Pololu_A1.1B, M1.D
  N7: Pololu_A1.1A, M1.B
  N8: Pololu_A1.2A, M1.A
  N9: Pololu_A1.2B, M1.C

custom parts:
  LPD8806 RGB LED Strip: Digitally addressable RGB LED strip
